// Logisim project One's Count.circ as structural Verilog: 1 circuit, main circuit main
module main (
  input  [3:0] in_1,
  input  in_2,
  input  in_3,
  input  in_4,
  input  Enter_the_Data,
  input  in_6,
  input  in_7,
  input  in_8,
  input  in_9,
  input  Start,
  input  in_11,
  input  Reset,
  output [3:0] Counter_Output
);

  wire and_1_out, and_2_out, and_3_out, and_4_out, and_5_out, and_6_out, clock_1_out, G0_q, G1_q, G2_q,
       nor_1_out, not_1_out, not_2_out, or_1_out, or_2_out, R1_out, R1_q0, R1_q1, R1_q2, R1_q3, R1_q4, R1_q5,
       R1_q6, R1_q7;

  not not_1 (not_1_out, Start);
  not not_2 (not_2_out, nor_1_out);
  and and_1 (and_1_out, G1_q, not_2_out);
  and and_2 (and_2_out, G0_q, not_1_out);
  and and_3 (and_3_out, G1_q, nor_1_out);
  and and_4 (and_4_out, G0_q, Start);
  or or_1 (or_1_out, and_2_out, and_3_out);
  or or_2 (or_2_out, and_4_out, G2_q);
  Clock clock_1 (.out(clock_1_out));
  D_Flip_Flop G0 (.clk(clock_1_out), .D(or_1_out), .Q(G0_q), .preset(Reset));  // open: Qn, en, reset
  D_Flip_Flop G1 (.clk(clock_1_out), .D(or_2_out), .Q(G1_q), .reset(Reset));  // open: Qn, preset, en
  D_Flip_Flop G2 (.clk(clock_1_out), .D(and_1_out), .Q(G2_q), .reset(Reset));  // open: Qn, preset, en
  LED Ready (.in(G0_q));
  and and_5 (and_5_out, G0_q, Start);
  and and_6 (and_6_out, G1_q, R1_out, R1_out, not_2_out);
  LED led_1 (.in(and_5_out));
  LED Inrc_R2 (.in(and_6_out));
  LED Shift_R1 (.in(G2_q));
  Counter #(.width(4), .max('hf)) R2 (
    .load(and_5_out), .D(in_1), .count(and_6_out), .Q(Counter_Output), .clk(clock_1_out));  // open: carry, clr
  Shift_Register R1 (
    .shift(G2_q), .in(in_11), .clk(clock_1_out), .out(R1_out), .load(and_5_out), .d0(in_2), .q0(R1_q0),
    .d1(in_3), .q1(R1_q1), .d2(in_4), .q2(R1_q2), .d3(Enter_the_Data), .q3(R1_q3), .d4(in_6), .q4(R1_q4),
    .d5(in_7), .q5(R1_q5), .d6(in_8), .q6(R1_q6), .d7(in_9), .q7(R1_q7));  // open: clr
  nor nor_1 (nor_1_out, R1_q0, R1_q1, R1_q2, R1_q3, R1_q4, R1_q5, R1_q6, R1_q7);

  // Notes on the sheet:
  //   Start
  //   One
  //   R1_zero
  //   Controller Part 
  //   CLK
  //   One's Counter
  //   One-Hot Design 
  //   Load_Regs
  //   DataPath
endmodule
